# Fritzing sketch Fritzing-sketch (saved by Fritzing 0.9.3b)
circuit board: 8.46667cm x 5.64444cm
perfboards: 1

parts:
  J1 = female pin header, 8 pins [form="♀ (female)"]
  J2 = female pin header, 8 pins [form="♀ (female)"]
  J5 = screw terminal, 3 pins
  J3 = screw terminal, 3 pins
  J4 = screw terminal, 3 pins
  Part1 = Soil Moisture Sensor
  R1 = Resistor [tolerance=±5% resistance=220 package=THT]
  S1 = Pushbutton [package="[THT]"]
  M1 = DC Motor  # not connected
  R2 = Resistor [tolerance=±5% resistance=10k package=THT]  # not connected

nets:
  N1: J1.pin4, J4.pin2
  N2: J1.pin5, J1.pin7, J4.pin3, S1.Pin_3, S1.Pin_4
  N3: J1.pin6, J5.pin1, Part1.VCC
  N4: J1.pin8, J2.pin1, J3.pin1, J3.pin3, J4.pin1, R1.Pin_0
  N5: J2.pin2, J5.pin3, Part1.SIG
  N6: R1.Pin_1, S1.Pin_1, S1.Pin_2

notes:
  YL-69
  Relay [NO]
